# Fritzing sketch lampu otomatis (saved by Fritzing 0.9.5d)

parts:
  FC-1 = Sound Sensor
  Part1 = Arduino Nano (Rev3.0) (ICSP)
  Mod1 = KY-019 5V Relay Module [package="Breakout board"]

nets:
  VCC: FC-1.VCC, Part1.5V
  GND: FC-1.GND, Part1.GND, Mod1.-
  N1: FC-1.OUT, Part1.D2
  N2: Part1.D12/MISO, Mod1.S

notes:
  relay sebagai saklar

custom parts:
  KY-019 5V Relay Module: KY-019 5V Relay module, used to control AC circuits. (Special thanks to vanepp for fixing the PCB holes and other errors)
